// Logisim project CPU.circ as structural Verilog: 17 circuits, main circuit CPU
module CPU (
  input  enabler,
  input  Reset,
  input  Interrupt,
  input  HaltRun,
  output [15:0] output_a,
  output [15:0] output_b
);

  wire clock_1_out, parsecontrolrom_1_alusrc, parsecontrolrom_1_memread, parsecontrolrom_1_memtoreg,
       parsecontrolrom_1_memwrite, parsecontrolrom_1_regwrite;
  wire [2:0] parsecontrolrom_1_opcode;
  wire [3:0] parseir_1_destreg, parseir_1_immorsrc2, parseir_1_opcode, parseir_1_srcreg1;
  wire [8:0] ControlROM_data;
  wire [15:0] alu_1_o, bit_extender_1_out, InstructionRegister_q, InstructionROM_data, multiplexer_1_out,
       multiplexer_2_out, pc_1_o, ram_1_dout;

  Clock clock_1 (.out(clock_1_out));
  ROM #(.addrWidth(16), .dataWidth(16)) InstructionROM (.addr(pc_1_o), .data(InstructionROM_data));
  PC pc_1 (.jump_e(enabler), .clock(clock_1_out), .reset(Reset), .O(pc_1_o));  // open: jump_addr
  Register #(.width(16)) InstructionRegister (
    .D(InstructionROM_data), .en(1'b1), .clk(clock_1_out), .Q(InstructionRegister_q), .clr(Reset));
  ParseIR parseir_1 (
    .IR(InstructionRegister_q), .OPCode(parseir_1_opcode), .DestReg(parseir_1_destreg),
    .SrcReg1(parseir_1_srcreg1), .ImmOrSrc2(parseir_1_immorsrc2));
  ROM #(.addrWidth(4), .dataWidth(9)) ControlROM (.addr(parseir_1_opcode), .data(ControlROM_data));
  assign bit_extender_1_out = {{12{parseir_1_immorsrc2[3]}}, parseir_1_immorsrc2};  // Bit_Extender bit_extender_1
  Multiplexer #(.width(16)) multiplexer_1 (
    .in0(alu_1_o), .in1(ram_1_dout), .out(multiplexer_1_out), .sel(parsecontrolrom_1_memtoreg));
  parseControlROM parsecontrolrom_1 (
    .in_1(ControlROM_data), .OPCode(parsecontrolrom_1_opcode), .Regwrite(parsecontrolrom_1_regwrite),
    .MemRead(parsecontrolrom_1_memread), .MemWrite(parsecontrolrom_1_memwrite),
    .MemToReg(parsecontrolrom_1_memtoreg), .ALUSRC(parsecontrolrom_1_alusrc));  // open: Branch
  Multiplexer #(.width(16)) multiplexer_2 (
    .in0(output_b), .in1(bit_extender_1_out), .out(multiplexer_2_out), .sel(parsecontrolrom_1_alusrc));
  RegFile regfile_1 (
    .readRegister1(parseir_1_srcreg1), .readRegister2(parseir_1_immorsrc2),
    .writeReg_addr(parseir_1_destreg), .writeData(multiplexer_1_out),
    .regWriteEnabler(parsecontrolrom_1_regwrite), .Reset(Reset), .clock(clock_1_out), .read_a(output_a),
    .read_b(output_b));
  ALU alu_1 (.A(output_a), .B(multiplexer_2_out), .Opcode(parsecontrolrom_1_opcode), .O(alu_1_o));
  RAM #(.addrWidth(16), .dataWidth(16)) ram_1 (
    .addr(alu_1_o), .we(parsecontrolrom_1_memwrite), .oe(parsecontrolrom_1_memread), .clk(clock_1_out),
    .din(output_b), .dout(ram_1_dout));

  // Notes on the sheet:
  //   contents of InstructionROM (hex, n*v repeats v):
  //   6105 6206 321 7307 6407 8340 9000
  //   contents of ControlROM (hex, n*v repeats v):
  //   c0 c1 c2 c3 c4 c5 c6 c7 c8 c9 1b0 1c0
endmodule

module PC (
  input  [15:0] jump_addr,
  input  jump_e,
  input  clock,
  input  reset,
  output [15:0] O
);

  wire [15:0] multiplexer_1_out, sixteenbitadder_1_o;

  sixteenbitadder sixteenbitadder_1 (.Cin(1'b1), .A(O), .O(sixteenbitadder_1_o));  // open: B, Cout
  Multiplexer #(.width(16)) multiplexer_1 (
    .in0(sixteenbitadder_1_o), .in1(jump_addr), .out(multiplexer_1_out), .sel(jump_e));
  Register #(.width(16)) register_1 (.D(multiplexer_1_out), .en(1'b1), .clk(clock), .Q(O), .clr(reset));
endmodule

module sixteenbitadder (
  input  Cin,
  input  [15:0] A,
  input  [15:0] B,
  output [15:0] O,
  output Cout
);

  wire fourbitadder_1_cout, fourbitadder_2_cout, fourbitadder_3_cout;

  fourbitadder fourbitadder_1 (.Cin(Cin), .A(A[3:0]), .B(B[3:0]), .O(O[3:0]), .Cout(fourbitadder_1_cout));
  fourbitadder fourbitadder_2 (
    .Cin(fourbitadder_1_cout), .A(A[7:4]), .B(B[7:4]), .O(O[7:4]), .Cout(fourbitadder_2_cout));
  fourbitadder fourbitadder_3 (
    .Cin(fourbitadder_2_cout), .A(A[11:8]), .B(B[11:8]), .O(O[11:8]), .Cout(fourbitadder_3_cout));
  fourbitadder fourbitadder_4 (.Cin(fourbitadder_3_cout), .A(A[15:12]), .B(B[15:12]), .O(O[15:12]), .Cout(Cout));
endmodule

module fourbitadder (
  input  Cin,
  input  [3:0] A,
  input  [3:0] B,
  output [3:0] O,
  output Cout
);

  wire fulladder_1_cout, fulladder_2_cout, fulladder_3_cout;

  fulladder fulladder_1 (.Cin(Cin), .A(A[0]), .B(B[0]), .O(O[0]), .Cout(fulladder_1_cout));
  fulladder fulladder_2 (.Cin(fulladder_1_cout), .A(A[1]), .B(B[1]), .O(O[1]), .Cout(fulladder_2_cout));
  fulladder fulladder_3 (.Cin(fulladder_2_cout), .A(A[2]), .B(B[2]), .O(O[2]), .Cout(fulladder_3_cout));
  fulladder fulladder_4 (.Cin(fulladder_3_cout), .A(A[3]), .B(B[3]), .O(O[3]), .Cout(Cout));
endmodule

module halfadder (
  input  A,
  input  B,
  output O,
  output Cout
);

  xor xor_1 (O, A, B);
  and and_1 (Cout, A, B);
endmodule

module fulladder (
  input  Cin,
  input  A,
  input  B,
  output O,
  output Cout
);

  wire halfadder_1_cout, halfadder_2_cout, halfadder_2_o;

  halfadder halfadder_1 (.A(Cin), .B(halfadder_2_o), .O(O), .Cout(halfadder_1_cout));
  halfadder halfadder_2 (.A(A), .B(B), .O(halfadder_2_o), .Cout(halfadder_2_cout));
  or or_1 (Cout, halfadder_1_cout, halfadder_2_cout);
endmodule

module RegFile (
  input  [3:0] readRegister1,
  input  [3:0] readRegister2,
  input  [3:0] writeReg_addr,
  input  [15:0] writeData,
  input  regWriteEnabler,
  input  Reset,
  input  clock,
  output [15:0] read_a,
  output [15:0] read_b
);

  wire decoder_1_out0, decoder_1_out1, decoder_1_out2, decoder_1_out3, decoder_1_out4, decoder_1_out5,
       decoder_1_out6, decoder_1_out7, decoder_1_out8, decoder_1_out9, decoder_1_out10, decoder_1_out11,
       decoder_1_out12, decoder_1_out13, decoder_1_out14, decoder_1_out15, decoder_2_out0, decoder_2_out1,
       decoder_2_out2, decoder_2_out3, decoder_2_out4, decoder_2_out5, decoder_2_out6, decoder_2_out7,
       decoder_2_out8, decoder_2_out9, decoder_2_out10, decoder_2_out11, decoder_2_out12, decoder_2_out13,
       decoder_2_out14, decoder_2_out15, decoder_3_out0, decoder_3_out1, decoder_3_out2, decoder_3_out3,
       decoder_3_out4, decoder_3_out5, decoder_3_out6, decoder_3_out7, decoder_3_out8, decoder_3_out9,
       decoder_3_out10, decoder_3_out11, decoder_3_out12, decoder_3_out13, decoder_3_out14, decoder_3_out15;
  wire [15:0] reg0_q, reg1_q, reg2_q, reg3_q, reg4_q, reg5_q, reg6_q, reg7_q, reg8_q, reg9_q, reg10_q,
       reg11_q, reg12_q, reg13_q, reg15_q, rqg14_q;

  Decoder #(.enable("false"), .select(4)) decoder_1 (
    .out0(decoder_1_out0), .out1(decoder_1_out1), .out2(decoder_1_out2), .out3(decoder_1_out3),
    .out4(decoder_1_out4), .out5(decoder_1_out5), .out6(decoder_1_out6), .out7(decoder_1_out7),
    .out8(decoder_1_out8), .out9(decoder_1_out9), .out10(decoder_1_out10), .out11(decoder_1_out11),
    .out12(decoder_1_out12), .out13(decoder_1_out13), .out14(decoder_1_out14), .out15(decoder_1_out15),
    .sel(readRegister1));
  Decoder #(.enable("false"), .select(4)) decoder_2 (
    .out0(decoder_2_out0), .out1(decoder_2_out1), .out2(decoder_2_out2), .out3(decoder_2_out3),
    .out4(decoder_2_out4), .out5(decoder_2_out5), .out6(decoder_2_out6), .out7(decoder_2_out7),
    .out8(decoder_2_out8), .out9(decoder_2_out9), .out10(decoder_2_out10), .out11(decoder_2_out11),
    .out12(decoder_2_out12), .out13(decoder_2_out13), .out14(decoder_2_out14), .out15(decoder_2_out15),
    .sel(readRegister2));
  Decoder #(.select(4)) decoder_3 (
    .out0(decoder_3_out0), .out1(decoder_3_out1), .out2(decoder_3_out2), .out3(decoder_3_out3),
    .out4(decoder_3_out4), .out5(decoder_3_out5), .out6(decoder_3_out6), .out7(decoder_3_out7),
    .out8(decoder_3_out8), .out9(decoder_3_out9), .out10(decoder_3_out10), .out11(decoder_3_out11),
    .out12(decoder_3_out12), .out13(decoder_3_out13), .out14(decoder_3_out14), .out15(decoder_3_out15),
    .sel(writeReg_addr), .en(regWriteEnabler));
  Register #(.width(16)) reg0 (.D(writeData), .en(decoder_3_out0), .clk(clock), .Q(reg0_q), .clr(Reset));
  Register #(.width(16)) reg1 (.D(writeData), .en(decoder_3_out1), .clk(clock), .Q(reg1_q), .clr(Reset));
  Register #(.width(16)) reg2 (.D(writeData), .en(decoder_3_out2), .clk(clock), .Q(reg2_q), .clr(Reset));
  Register #(.width(16)) reg3 (.D(writeData), .en(decoder_3_out3), .clk(clock), .Q(reg3_q), .clr(Reset));
  Register #(.width(16)) reg4 (.D(writeData), .en(decoder_3_out4), .clk(clock), .Q(reg4_q), .clr(Reset));
  Register #(.width(16)) reg5 (.D(writeData), .en(decoder_3_out5), .clk(clock), .Q(reg5_q), .clr(Reset));
  Register #(.width(16)) reg6 (.D(writeData), .en(decoder_3_out6), .clk(clock), .Q(reg6_q), .clr(Reset));
  Register #(.width(16)) reg7 (.D(writeData), .en(decoder_3_out7), .clk(clock), .Q(reg7_q), .clr(Reset));
  assign read_b = decoder_2_out0 ? reg0_q : 16'bz;  // Controlled_Buffer controlled_buffer_1
  Register #(.width(16)) reg8 (.D(writeData), .en(decoder_3_out8), .clk(clock), .Q(reg8_q), .clr(Reset));
  Register #(.width(16)) reg9 (.D(writeData), .en(decoder_3_out9), .clk(clock), .Q(reg9_q), .clr(Reset));
  Register #(.width(16)) reg10 (.D(writeData), .en(decoder_3_out10), .clk(clock), .Q(reg10_q), .clr(Reset));
  Register #(.width(16)) reg11 (.D(writeData), .en(decoder_3_out11), .clk(clock), .Q(reg11_q), .clr(Reset));
  Register #(.width(16)) reg12 (.D(writeData), .en(decoder_3_out12), .clk(clock), .Q(reg12_q), .clr(Reset));
  Register #(.width(16)) reg13 (.D(writeData), .en(decoder_3_out13), .clk(clock), .Q(reg13_q), .clr(Reset));
  Register #(.width(16)) rqg14 (.D(writeData), .en(decoder_3_out14), .clk(clock), .Q(rqg14_q), .clr(Reset));
  Register #(.width(16)) reg15 (.D(writeData), .en(decoder_3_out15), .clk(clock), .Q(reg15_q), .clr(Reset));
  assign read_b = decoder_2_out7 ? reg7_q : 16'bz;  // Controlled_Buffer controlled_buffer_2
  assign read_b = decoder_2_out1 ? reg1_q : 16'bz;  // Controlled_Buffer controlled_buffer_3
  assign read_a = decoder_1_out8 ? reg8_q : 16'bz;  // Controlled_Buffer controlled_buffer_4
  assign read_b = decoder_2_out8 ? reg8_q : 16'bz;  // Controlled_Buffer controlled_buffer_5
  assign read_a = decoder_1_out1 ? reg1_q : 16'bz;  // Controlled_Buffer controlled_buffer_6
  assign read_a = decoder_1_out9 ? reg9_q : 16'bz;  // Controlled_Buffer controlled_buffer_7
  assign read_b = decoder_2_out9 ? reg9_q : 16'bz;  // Controlled_Buffer controlled_buffer_8
  assign read_a = decoder_1_out2 ? reg2_q : 16'bz;  // Controlled_Buffer controlled_buffer_9
  assign read_a = decoder_1_out10 ? reg10_q : 16'bz;  // Controlled_Buffer controlled_buffer_10
  assign read_b = decoder_2_out2 ? reg2_q : 16'bz;  // Controlled_Buffer controlled_buffer_11
  assign read_a = decoder_1_out3 ? reg3_q : 16'bz;  // Controlled_Buffer controlled_buffer_12
  assign read_a = decoder_1_out11 ? reg11_q : 16'bz;  // Controlled_Buffer controlled_buffer_13
  assign read_a = decoder_1_out4 ? reg4_q : 16'bz;  // Controlled_Buffer controlled_buffer_14
  assign read_a = decoder_1_out12 ? reg12_q : 16'bz;  // Controlled_Buffer controlled_buffer_15
  assign read_b = decoder_2_out12 ? reg12_q : 16'bz;  // Controlled_Buffer controlled_buffer_16
  assign read_a = decoder_1_out5 ? reg5_q : 16'bz;  // Controlled_Buffer controlled_buffer_17
  assign read_a = decoder_1_out13 ? reg13_q : 16'bz;  // Controlled_Buffer controlled_buffer_18
  assign read_a = decoder_1_out6 ? reg6_q : 16'bz;  // Controlled_Buffer controlled_buffer_19
  assign read_a = decoder_1_out14 ? rqg14_q : 16'bz;  // Controlled_Buffer controlled_buffer_20
  assign read_a = decoder_1_out7 ? reg7_q : 16'bz;  // Controlled_Buffer controlled_buffer_21
  assign read_a = decoder_1_out15 ? reg15_q : 16'bz;  // Controlled_Buffer controlled_buffer_22
  assign read_a = decoder_1_out0 ? reg0_q : 16'bz;  // Controlled_Buffer controlled_buffer_23
  assign read_b = decoder_2_out10 ? reg10_q : 16'bz;  // Controlled_Buffer controlled_buffer_24
  assign read_b = decoder_2_out13 ? reg13_q : 16'bz;  // Controlled_Buffer controlled_buffer_25
  assign read_b = decoder_2_out4 ? reg4_q : 16'bz;  // Controlled_Buffer controlled_buffer_26
  assign read_b = decoder_2_out15 ? reg15_q : 16'bz;  // Controlled_Buffer controlled_buffer_27
  assign read_b = decoder_2_out6 ? reg6_q : 16'bz;  // Controlled_Buffer controlled_buffer_28
  assign read_b = decoder_2_out11 ? reg11_q : 16'bz;  // Controlled_Buffer controlled_buffer_29
  assign read_b = decoder_2_out3 ? reg3_q : 16'bz;  // Controlled_Buffer controlled_buffer_30
  assign read_b = decoder_2_out14 ? rqg14_q : 16'bz;  // Controlled_Buffer controlled_buffer_31
  assign read_b = decoder_2_out5 ? reg5_q : 16'bz;  // Controlled_Buffer controlled_buffer_32
endmodule

module ALU (
  input  [15:0] A,
  input  [15:0] B,
  input  [2:0] Opcode,
  output [15:0] O
);

  wire [15:0] sixteenbitadder_1_o, sixteenbitbitwiseand_1_o, sixteenbitbitwiseor_1_o,
       sixteenbitshiftleft_1_o, sixteenbitshiftright_1_o, sixteenbitslt_1_o, sixteenbitsubtractor_1_o,
       sixteenbitxorgate_1_o;

  sixteenbitadder sixteenbitadder_1 (.A(A), .B(B), .O(sixteenbitadder_1_o));  // open: Cin, Cout
  sixteenbitsubtractor sixteenbitsubtractor_1 (.A(A), .B(B), .O(sixteenbitsubtractor_1_o));  // open: Cout
  sixteenbitbitwiseAnd sixteenbitbitwiseand_1 (.A(A), .B(B), .O(sixteenbitbitwiseand_1_o));
  sixteenbitbitwiseOR sixteenbitbitwiseor_1 (.A(A), .B(B), .O(sixteenbitbitwiseor_1_o));
  sixteenbitXorGate sixteenbitxorgate_1 (.A(A), .B(B), .O(sixteenbitxorgate_1_o));
  sixteenbitSLT sixteenbitslt_1 (.A(A), .B(B), .O(sixteenbitslt_1_o));
  sixteenbitshiftleft sixteenbitshiftleft_1 (.B(B), .O(sixteenbitshiftleft_1_o));
  sixteenbitshiftright sixteenbitshiftright_1 (.B(B), .O(sixteenbitshiftright_1_o));
  Multiplexer #(.select(3), .width(16)) multiplexer_1 (
    .in0(sixteenbitadder_1_o), .in1(sixteenbitsubtractor_1_o), .in2(sixteenbitbitwiseand_1_o),
    .in3(sixteenbitbitwiseor_1_o), .in4(sixteenbitxorgate_1_o), .in5(sixteenbitslt_1_o),
    .in6(sixteenbitshiftleft_1_o), .in7(sixteenbitshiftright_1_o), .out(O), .sel(Opcode));
endmodule

module sixteenbitsubtractor (
  input  [15:0] A,
  input  [15:0] B,
  output [15:0] O,
  output Cout
);

  wire [15:0] not_1_out;

  assign not_1_out = ~B;  // NOT_Gate not_1, 16 bits wide
  sixteenbitadder sixteenbitadder_1 (.Cin(1'b1), .A(A), .B(not_1_out), .O(O), .Cout(Cout));
endmodule

module sixteenbitbitwiseAnd (
  input  [15:0] A,
  input  [15:0] B,
  output [15:0] O
);

  assign O = A & B;  // AND_Gate and_1, 16 bits wide
endmodule

module sixteenbitbitwiseOR (
  input  [15:0] A,
  input  [15:0] B,
  output [15:0] O
);

  assign O = A | B;  // OR_Gate or_1, 16 bits wide
endmodule

module sixteenbitXorGate (
  input  [15:0] A,
  input  [15:0] B,
  output [15:0] O
);

  assign O = A ^ B;  // XOR_Gate xor_1, 16 bits wide
endmodule

module sixteenbitSLT (
  input  [15:0] A,
  input  [15:0] B,
  output [15:0] O
);

  wire [14:0] sixteenbitsubtractor_1_o;

  sixteenbitsubtractor sixteenbitsubtractor_1 (.A(A), .B(B), .O({O[0], sixteenbitsubtractor_1_o}));  // open: Cout

  assign O[15:1] = {15{1'b0}};
endmodule

module sixteenbitshiftright (
  input  [15:0] B,
  output [15:0] O
);

  wire and_1_out, and_2_out, and_3_out, and_4_out, and_5_out, and_6_out, and_7_out, and_8_out, and_9_out,
       and_10_out, and_11_out, and_12_out, and_13_out, and_14_out, and_15_out, and_16_out, and_17_out,
       and_18_out, and_19_out, and_20_out, and_21_out, and_22_out, and_23_out, and_24_out, and_25_out,
       and_26_out, and_27_out, and_28_out, and_29_out, and_30_out, and_31_out, and_32_out, not_1_out,
       not_2_out, not_3_out, not_4_out, not_5_out, not_6_out, not_7_out, not_8_out, not_9_out, not_10_out,
       not_11_out, not_12_out, not_13_out, not_14_out, not_15_out, not_16_out;

  and and_1 (and_1_out, 1'b0, 1'b1);
  not not_1 (not_1_out, 1'b1);
  and and_2 (and_2_out, B[15], not_1_out);
  xor xor_1 (O[15], and_1_out, and_2_out);
  and and_3 (and_3_out, B[15], 1'b1);
  xor xor_2 (O[14], and_3_out, and_4_out);
  not not_2 (not_2_out, 1'b1);
  and and_4 (and_4_out, B[14], not_2_out);
  and and_5 (and_5_out, B[14], 1'b1);
  not not_3 (not_3_out, 1'b1);
  and and_6 (and_6_out, B[13], not_3_out);
  xor xor_3 (O[13], and_5_out, and_6_out);
  and and_7 (and_7_out, B[13], 1'b1);
  xor xor_4 (O[12], and_7_out, and_8_out);
  not not_4 (not_4_out, 1'b1);
  and and_8 (and_8_out, B[12], not_4_out);
  and and_9 (and_9_out, B[12], 1'b1);
  not not_5 (not_5_out, 1'b1);
  and and_10 (and_10_out, B[11], not_5_out);
  xor xor_5 (O[11], and_9_out, and_10_out);
  and and_11 (and_11_out, B[11], 1'b1);
  xor xor_6 (O[10], and_11_out, and_12_out);
  not not_6 (not_6_out, 1'b1);
  and and_12 (and_12_out, B[10], not_6_out);
  and and_13 (and_13_out, B[10], 1'b1);
  not not_7 (not_7_out, 1'b1);
  and and_14 (and_14_out, B[9], not_7_out);
  xor xor_7 (O[9], and_13_out, and_14_out);
  and and_15 (and_15_out, B[9], 1'b1);
  xor xor_8 (O[8], and_15_out, and_16_out);
  not not_8 (not_8_out, 1'b1);
  and and_16 (and_16_out, B[8], not_8_out);
  and and_17 (and_17_out, B[8], 1'b1);
  not not_9 (not_9_out, 1'b1);
  and and_18 (and_18_out, B[7], not_9_out);
  xor xor_9 (O[7], and_17_out, and_18_out);
  and and_19 (and_19_out, B[7], 1'b1);
  xor xor_10 (O[6], and_19_out, and_20_out);
  not not_10 (not_10_out, 1'b1);
  and and_20 (and_20_out, B[6], not_10_out);
  and and_21 (and_21_out, B[6], 1'b1);
  not not_11 (not_11_out, 1'b1);
  and and_22 (and_22_out, B[5], not_11_out);
  xor xor_11 (O[5], and_21_out, and_22_out);
  and and_23 (and_23_out, B[5], 1'b1);
  xor xor_12 (O[4], and_23_out, and_24_out);
  not not_12 (not_12_out, 1'b1);
  and and_24 (and_24_out, B[4], not_12_out);
  and and_25 (and_25_out, B[4], 1'b1);
  not not_13 (not_13_out, 1'b1);
  and and_26 (and_26_out, B[3], not_13_out);
  xor xor_13 (O[3], and_25_out, and_26_out);
  and and_27 (and_27_out, B[3], 1'b1);
  xor xor_14 (O[2], and_27_out, and_28_out);
  not not_14 (not_14_out, 1'b1);
  and and_28 (and_28_out, B[2], not_14_out);
  and and_29 (and_29_out, B[2], 1'b1);
  not not_15 (not_15_out, 1'b1);
  and and_30 (and_30_out, B[1], not_15_out);
  xor xor_15 (O[1], and_29_out, and_30_out);
  and and_31 (and_31_out, B[1], 1'b1);
  xor xor_16 (O[0], and_31_out, and_32_out);
  not not_16 (not_16_out, 1'b1);
  and and_32 (and_32_out, B[0], not_16_out);
endmodule

module sixteenbitshiftleft (
  input  [15:0] B,
  output [15:0] O
);

  wire and_1_out, and_2_out, and_3_out, and_4_out, and_5_out, and_6_out, and_7_out, and_8_out, and_9_out,
       and_10_out, and_11_out, and_12_out, and_13_out, and_14_out, and_15_out, and_16_out, and_17_out,
       and_18_out, and_19_out, and_20_out, and_21_out, and_22_out, and_23_out, and_24_out, and_25_out,
       and_26_out, and_27_out, and_28_out;

  and and_1 (and_1_out, 1'b1, B[14]);
  xor xor_1 (O[15], and_1_out, and_2_out);
  and and_2 (and_2_out, 1'b0, B[14]);
  and and_3 (and_3_out, 1'b1, B[13]);
  and and_4 (and_4_out, 1'b0, B[13]);
  xor xor_2 (O[14], and_3_out, and_4_out);
  and and_5 (and_5_out, 1'b1, B[12]);
  xor xor_3 (O[13], and_5_out, and_6_out);
  and and_6 (and_6_out, 1'b0, B[12]);
  and and_7 (and_7_out, 1'b1, B[11]);
  and and_8 (and_8_out, 1'b0, B[11]);
  xor xor_4 (O[12], and_7_out, and_8_out);
  and and_9 (and_9_out, 1'b1, B[10]);
  xor xor_5 (O[11], and_9_out, and_10_out);
  and and_10 (and_10_out, 1'b0, B[10]);
  and and_11 (and_11_out, 1'b1, B[9]);
  and and_12 (and_12_out, 1'b0, B[9]);
  xor xor_6 (O[10], and_11_out, and_12_out);
  and and_13 (and_13_out, 1'b1, B[8]);
  xor xor_7 (O[9], and_13_out, and_14_out);
  and and_14 (and_14_out, 1'b0, B[8]);
  and and_15 (and_15_out, 1'b1, B[7]);
  and and_16 (and_16_out, 1'b0, B[7]);
  xor xor_8 (O[8], and_15_out, and_16_out);
  and and_17 (and_17_out, 1'b1, B[6]);
  xor xor_9 (O[7], and_17_out, and_18_out);
  and and_18 (and_18_out, 1'b0, B[6]);
  and and_19 (and_19_out, 1'b1, B[5]);
  and and_20 (and_20_out, 1'b0, B[5]);
  xor xor_10 (O[6], and_19_out, and_20_out);
  and and_21 (and_21_out, 1'b1, B[4]);
  xor xor_11 (O[5], and_21_out, and_22_out);
  and and_22 (and_22_out, 1'b0, B[4]);
  and and_23 (and_23_out, 1'b1, B[3]);
  and and_24 (and_24_out, 1'b0, B[3]);
  xor xor_12 (O[4], and_23_out, and_24_out);
  and and_25 (and_25_out, 1'b1, B[2]);
  xor xor_13 (O[3], and_25_out, and_26_out);
  and and_26 (and_26_out, 1'b0, B[2]);
  and and_27 (and_27_out, 1'b1, B[1]);
  and and_28 (and_28_out, 1'b0, B[1]);
  xor xor_14 (O[2], and_27_out, and_28_out);
  and and_29 (O[1], B[0], 1'b1);

  assign O[0] = 1'b0;
endmodule

module ParseIR (
  input  [15:0] IR,
  output [3:0] OPCode,
  output [3:0] DestReg,
  output [3:0] SrcReg1,
  output [3:0] ImmOrSrc2
);


  assign DestReg = IR[11:8];
  assign ImmOrSrc2 = IR[3:0];
  assign OPCode = IR[15:12];
  assign SrcReg1 = IR[7:4];
endmodule

module parseControlROM (
  input  [8:0] in_1,
  output [2:0] OPCode,
  output Regwrite,
  output MemRead,
  output MemWrite,
  output MemToReg,
  output ALUSRC,
  output Branch
);


  assign ALUSRC = in_1[1];
  assign Branch = in_1[0];
  assign MemRead = in_1[4];
  assign MemToReg = in_1[2];
  assign MemWrite = in_1[3];
  assign OPCode = in_1[8:6];
  assign Regwrite = in_1[5];
endmodule
